// Digital circuit Ampel_Einfach.dig as structural Verilog
module Ampel_Einfach (
  input  Clock
);

  wire and_1_out, Z_0_nq, Z_0_q, Z_1_nq, Z_1_q;

  JK_FF Z_1 (.J(Z_0_q), .C(Clock), .K(Z_0_q), .Q(Z_1_q), .nQ(Z_1_nq));
  JK_FF Z_0 (.J(1'b1), .C(Clock), .K(1'b1), .Q(Z_0_q), .nQ(Z_0_nq));
  and and_1 (and_1_out, Z_1_q, Z_0_nq);
  LED Rot (.in(Z_1_nq));
  LED Gelb (.in(Z_0_q));
  LED \Grün  (.in(and_1_out));
endmodule
