// Digital circuit Count_JK.dig as structural Verilog
module Count_JK (
  input  clk,
  output Q0,
  output Q1,
  output Q2,
  output Q3
);

  wire and_1_out, and_2_out;

  JK_FF jk_ff_1 (.J(1'b1), .C(clk), .K(1'b1), .Q(Q0));  // open: nQ
  JK_FF jk_ff_2 (.J(Q0), .C(clk), .K(Q0), .Q(Q1));  // open: nQ
  and and_1 (and_1_out, Q0, Q1);
  JK_FF jk_ff_3 (.J(and_1_out), .C(clk), .K(and_1_out), .Q(Q2));  // open: nQ
  and and_2 (and_2_out, and_1_out, Q2);
  JK_FF jk_ff_4 (.J(and_2_out), .C(clk), .K(and_2_out), .Q(Q3));  // open: nQ
endmodule
