// Digital circuit d-tg-ff.dig as structural Verilog
module d_tg_ff (
  input  D,
  input  C,
  output nQ,
  output Q
);

  wire nfet_3_s, nfet_4_s, pfet_1_d, pfet_4_s, pullup_1_out;

  PFET pfet_1 (.G(C), .S(1'b1), .D(pfet_1_d));
  NFET nfet_1 (.G(C), .D(pfet_1_d), .S(1'b0));
  PFET pfet_2 (.G(pfet_1_d), .S(Q), .D(D));
  NFET nfet_2 (.G(C), .D(D), .S(Q));
  PullUp pullup_1 (.out(pullup_1_out));
  PFET pfet_3 (.G(Q), .S(pullup_1_out), .D(nQ));
  PFET pfet_4 (.G(nQ), .S(pfet_4_s), .D(Q));
  NFET nfet_3 (.G(Q), .D(nQ), .S(nfet_3_s));
  NFET nfet_4 (.G(nQ), .D(Q), .S(nfet_4_s));
  PullDown pulldown_1 (.out(nfet_3_s));
  PullUp pullup_2 (.out(pfet_4_s));
  PullDown pulldown_2 (.out(nfet_4_s));
endmodule

/* Test case:
C D Q ~Q
1 0 0 1
0 0 0 1
0 1 0 1
0 0 0 1
1 1 1 0
0 1 1 0
0 0 1 0
1 0 0 1
0 0 0 1
*/
