// Digital circuit Bus.dig as structural Verilog
// Einfache Schaltung die eine Adressdecodierung 
// zeigt. Der Zähler erzeugt eine 5-Bit Zahl.
// Die unteren drei Bit werden als Adresse an alle 
// ROM-Bausteine ausgegeben. Die oberen zwei Bits
// werden verwendet um über den Adressdecoder 
// einen der vier ROM-Bausteine auszuwählen, welcher dann
// sein Datenwort an den Datenbus legt. Durch den 
// Adressdecoder verhalten sich die vier ROM-Bausteine wie
// ein einziger viermal so großer ROM-Baustein.
// Alle Ausgänge der ROMs liegen auf einem Datenbus. Dies ist
// möglich, da immer nur der Ausgang eines der vier ROMs aktiv 
// ist. Die jeweils anderen Ausgänge sind hochohmig.
module Bus (
  input  Clock
);

  wire decoder_1_out_0, decoder_1_out_1, decoder_1_out_2, decoder_1_out_3;
  wire [4:0] Address_out;
  wire [7:0] rom_1_d;

  Counter #(.Bits(5)) Address (.en(Clock), .C(1'b0), .out(Address_out));  // open: clr, ovf
  Decoder #(.Selector_Bits(2)) decoder_1 (
    .sel(Address_out[4:3]), .out_0(decoder_1_out_0), .out_1(decoder_1_out_1), .out_2(decoder_1_out_2),
    .out_3(decoder_1_out_3));
  ROM #(.Bits(8), .Addr_Bits(3)) rom_1 (.A(Address_out[2:0]), .sel(decoder_1_out_0), .D(rom_1_d));
  ROM #(.Bits(8), .Addr_Bits(3)) rom_2 (.A(Address_out[2:0]), .sel(decoder_1_out_1), .D(rom_1_d));
  ROM #(.Bits(8), .Addr_Bits(3)) rom_3 (.A(Address_out[2:0]), .sel(decoder_1_out_2), .D(rom_1_d));
  ROM #(.Bits(8), .Addr_Bits(3)) rom_4 (.A(Address_out[2:0]), .sel(decoder_1_out_3), .D(rom_1_d));
  // Probe Data on rom_1_d

  // Notes on the sheet:
  //   Clock: Hz: 2
  //   contents of rom_1 (hex, n*v repeats v):
  //   8
  //   68
  //   105
  //   101
  //   115
  //   32
  //   105
  //   115
  //   116
  //   contents of rom_2 (hex, n*v repeats v):
  //   8
  //   32
  //   101
  //   105
  //   110
  //   32
  //   108
  //   97
  //   110
  //   contents of rom_3 (hex, n*v repeats v):
  //   8
  //   103
  //   101
  //   114
  //   32
  //   84
  //   101
  //   115
  //   116
  //   contents of rom_4 (hex, n*v repeats v):
  //   8
  //   116
  //   101
  //   120
  //   116
  //   46
  //   32
  //   32
  //   32
endmodule
