// Digital circuit Comp7485.dig as structural Verilog
// Komparator welcher der Funktion eines
// 74x85 entspricht. Die drei Eingänge mit den
// Vergleichsbits werden direkt wieder ausgegeben,
// wenn die jeweiligen P und Q-Bits übereinstimmen.
module Comp7485 (
  input  P_0,
  input  P_1,
  input  P_2,
  input  P_3,
  input  P_lt_Q_i,
  input  P_eq_Q_i,
  input  P_gt_Q_i,
  input  Q_0,
  input  Q_1,
  input  Q_2,
  input  Q_3,
  output P_lt_Q,
  output P_eq_Q,
  output P_gt_Q
);

  wire comprc_1_p_eq_q, comprc_1_p_gt_q, comprc_1_p_lt_q;

  CompRC comprc_1 (
    .P_3(P_3), .P_2(P_2), .P_1(P_1), .P_0(P_0), .Q_3(Q_3), .Q_2(Q_2), .Q_1(Q_1), .Q_0(Q_0),
    .P_lt_Q(comprc_1_p_lt_q), .P_eq_Q(comprc_1_p_eq_q), .P_gt_Q(comprc_1_p_gt_q));
  Multiplexer multiplexer_1 (.sel(comprc_1_p_eq_q), .in_0(comprc_1_p_lt_q), .in_1(P_lt_Q_i), .out(P_lt_Q));
  Multiplexer multiplexer_2 (.sel(comprc_1_p_eq_q), .in_0(comprc_1_p_eq_q), .in_1(P_eq_Q_i), .out(P_eq_Q));
  Multiplexer multiplexer_3 (.sel(comprc_1_p_eq_q), .in_0(comprc_1_p_gt_q), .in_1(P_gt_Q_i), .out(P_gt_Q));

  // Notes on the sheet:
  //   P_lt_Q_i: Das P<Q-Bit der Vorgängerschaltung. Wird direkt
  //   wieder Ausgegeben wenn die jeweiligen P und Q 
  //   Bits übereinstimmen.
  //   P_eq_Q_i: Das P=Q-Bit der Vorgängerschaltung. Wird direkt
  //   wieder Ausgegeben wenn die jeweiligen P und Q 
  //   Bits übereinstimmen.
  //   P_gt_Q_i: Das P>Q-Bit der Vorgängerschaltung. Wird direkt
  //   wieder Ausgegeben wenn die jeweiligen P und Q 
  //   Bits übereinstimmen.
  //   P_lt_Q: Das Bit ist Eins, wenn P<Q gilt.
  //   P_eq_Q: Das Bit ist Eins, wenn P=Q gilt.
  //   P_gt_Q: Das Bit ist Eins, wenn P>Q gilt.
endmodule

/* Test case:
            P<Q_i P=Q_i P>Q_i  P_3 P_2 P_1 P_0   Q_3 Q_2 Q_1 Q_0  P<Q             P=Q             P>Q
repeat(256)   0    1     0     bits(4,n>>4)      bits(4,n)        ((n>>4)<(n&15)) ((n>>4)=(n&15)) ((n>>4)>(n&15))
repeat(2<<(3+4))  bits(3,n)    bits(4,n>>3)      bits(4,n>>3)     bits(3,n)
*/
