// Digital circuit CompRC.dig as structural Verilog
module CompRC (
  input  P_3,
  input  P_2,
  input  P_1,
  input  P_0,
  input  Q_3,
  input  Q_2,
  input  Q_1,
  input  Q_0,
  output P_lt_Q,
  output P_eq_Q,
  output P_gt_Q
);

  wire compen_1_p_eq_q, compen_1_p_gt_q, compen_1_p_lt_q, compen_2_p_eq_q, compen_2_p_gt_q, compen_2_p_lt_q,
       compen_3_p_eq_q, compen_3_p_gt_q, compen_3_p_lt_q, compen_4_p_gt_q, compen_4_p_lt_q;

  CompEN compen_1 (
    .EN(1'b1), .P(P_3), .Q(Q_3), .P_lt_Q(compen_1_p_lt_q), .P_eq_Q(compen_1_p_eq_q), .P_gt_Q(compen_1_p_gt_q));
  CompEN compen_2 (
    .EN(compen_1_p_eq_q), .P(P_2), .Q(Q_2), .P_lt_Q(compen_2_p_lt_q), .P_eq_Q(compen_2_p_eq_q),
    .P_gt_Q(compen_2_p_gt_q));
  CompEN compen_3 (
    .EN(compen_2_p_eq_q), .P(P_1), .Q(Q_1), .P_lt_Q(compen_3_p_lt_q), .P_eq_Q(compen_3_p_eq_q),
    .P_gt_Q(compen_3_p_gt_q));
  CompEN compen_4 (
    .EN(compen_3_p_eq_q), .P(P_0), .Q(Q_0), .P_lt_Q(compen_4_p_lt_q), .P_eq_Q(P_eq_Q),
    .P_gt_Q(compen_4_p_gt_q));
  or or_1 (P_lt_Q, compen_1_p_lt_q, compen_2_p_lt_q, compen_3_p_lt_q, compen_4_p_lt_q);
  or or_2 (P_gt_Q, compen_1_p_gt_q, compen_2_p_gt_q, compen_3_p_gt_q, compen_4_p_gt_q);
endmodule
