// Digital circuit LUT.dig as structural Verilog
module LUT (
  input  A,
  input  B,
  output Y
);

  wire pullup_1_out, pullup_2_out, pullup_3_out, pullup_4_out;

  PullUp pullup_1 (.out(pullup_1_out));
  PullUp pullup_2 (.out(pullup_2_out));
  Switch S_1 (.A(1'b0), .B(pullup_2_out));
  Switch #(.Closed("true")) S_0 (.A(1'b0), .B(pullup_1_out));
  PullUp pullup_3 (.out(pullup_3_out));
  Switch S_2 (.A(1'b0), .B(pullup_3_out));
  PullUp pullup_4 (.out(pullup_4_out));
  Multiplexer #(.Selector_Bits(2)) multiplexer_1 (
    .sel({B, A}), .in_0(pullup_1_out), .in_1(pullup_2_out), .in_2(pullup_3_out), .in_3(pullup_4_out), .out(Y));
  Switch #(.Closed("true")) S_3 (.A(1'b0), .B(pullup_4_out));
endmodule

/* Test case:
A B Y
0 0 0
0 1 1
1 0 1
1 1 0
*/
