// Digital circuit barrelShifter.dig as structural Verilog
// Barrel-Shifter with selectable bit width.
// {{de Barrel-Shifter mit wählbarer Bitbreite.}}
module barrelShifter (
  input  [15:0] D_in,
  input  [3:0] sh,
  output [15:0] D
);

  shift_inc #(.generic("dataBits:=16; shiftBits:=int(4); circuit:=\"shift-fixed-left-inc.dig\"; if (isPresent(args)) { if (args.dir=\"right\") { circuit=\"shift-fixed-right-inc.dig\"; } else { if (args.dir=\"arith\") { circuit=\"shift-fixed-arith-right-inc.dig\"; } else { if (args.dir!=\"left\") { panic(\"only \\\"left\\\", \\\"right\\\" or \\\"arith\\\" is allowed as direction, not \\\"\"+args.dir+\"\\\"!\"); } } } dataBits=args.dataBits; shiftBits=bi")) shift_inc_1 (
    .D_in(D_in), .sh(sh), .D(D));
endmodule
