// Digital circuit 74238.dig as structural Verilog
// 3-line to 8-line decoder/demultiplexer
module _74238 (
  input  A,
  input  C,
  input  B,
  input  G,
  input  nGB,
  input  nGA,
  input  VCC,
  input  GND,
  output nY0,
  output nY1,
  output nY2,
  output nY3,
  output nY4,
  output nY5,
  output nY6,
  output nY7
);

  wire and_1_out, not_1_out, not_2_out;

  PowerSupply powersupply_1 (.VDD(VCC), .GND(GND));
  not not_1 (not_1_out, nGB);
  not not_2 (not_2_out, nGA);
  and and_1 (and_1_out, G, not_1_out, not_2_out);
  Demultiplexer #(.Selector_Bits(3)) demultiplexer_1 (
    .sel({C, B, A}), .in(and_1_out), .out_0(nY0), .out_1(nY1), .out_2(nY2), .out_3(nY3), .out_4(nY4),
    .out_5(nY5), .out_6(nY6), .out_7(nY7));

  // Notes on the sheet:
  //   A: pin 1
  //   C: pin 3
  //   B: pin 2
  //   G: pin 6
  //   nGB: pin 5
  //   nGA: pin 4
  //   nY0: pin 15
  //   nY1: pin 14
  //   nY2: pin 13
  //   nY3: pin 12
  //   nY4: pin 11
  //   nY5: pin 10
  //   nY6: pin 9
  //   nY7: pin 7
  //   VCC: pin 16, default 1
  //   GND: pin 8
endmodule
