// Digital circuit 7489.dig as structural Verilog
// 64-bit RAM
module _7489 (
  input  A0,
  input  A1,
  input  A2,
  input  A3,
  input  D1,
  input  D2,
  input  D3,
  input  D4,
  input  nWE,
  input  nME,
  input  VCC,
  input  GND,
  output S4,
  output S1,
  output S2,
  output S3
);

  wire and_1_out, or_1_out;
  wire [3:0] not_1_out, ramasync_q;

  PowerSupply powersupply_1 (.VDD(VCC), .GND(GND));
  and and_1 (and_1_out, ~nWE, ~nME);  // And
  RAMAsync #(.AddrBits(4), .Bits(4)) ramasync (
    .A({A3, A2, A1, A0}), .D({D4, D3, D2, D1}), .we(and_1_out), .Q(ramasync_q));
  or or_1 (or_1_out, and_1_out, nME);
  assign not_1_out = ~ramasync_q;  // Not not_1, 4 bits wide
  Multiplexer #(.Bits(4)) multiplexer_1 (.sel(or_1_out), .in_0(not_1_out), .in_1(4'b1111), .out({S4, S3, S2, S1}));

  // Notes on the sheet:
  //   S4: pin 11
  //   S1: pin 5
  //   S2: pin 7
  //   S3: pin 9
  //   A0: pin 1
  //   A1: pin 15
  //   A2: pin 14
  //   A3: pin 13
  //   D1: pin 4
  //   D2: pin 6
  //   D3: pin 10
  //   D4: pin 12
  //   nWE: pin 3
  //   nME: pin 2
  //   VCC: pin 16, default 1
  //   GND: pin 8
endmodule
