// Digital circuit Control.dig as structural Verilog
module Control (
  input  [6:0] Op,
  input  BRKen,
  output stPC,
  output WE,
  output imm,
  output absJmp,
  output BRK,
  output [2:0] muxB,
  output muxA,
  output ALUToBus,
  output [4:0] ALUop,
  output [2:0] Branch,
  output st,
  output ld,
  output ioW,
  output ioR
);

  wire not_1_out;
  wire [5:0] multiplexer_1_out;
  wire [23:20] Logic_d;

  Multiplexer #(.Bits(6)) multiplexer_1 (.sel(Op[6]), .in_0(Op[5:0]), .in_1({6{1'b0}}), .out(multiplexer_1_out));
  ROM #(.Bits(24), .Addr_Bits(6)) Logic (
    .A(multiplexer_1_out), .sel(1'b1),
    .D({Logic_d, ioR, ioW, Branch, ALUop, muxA, stPC, WE, ALUToBus, absJmp, muxB, st, ld}));
  and and_1 (BRK, Logic_d[20], not_1_out);
  not not_1 (not_1_out, BRKen);

  assign imm = Op[6];

  // Notes on the sheet:
  //   contents of Logic (hex, n*v repeats v):
  //   64
  //   0
  //   192
  //   1216
  //   17600
  //   2240
  //   18624
  //   3264
  //   4288
  //   5312
  //   196
  //   212
  //   1220
  //   1236
  //   17604
  //   17620
  //   2244
  //   2260
  //   18628
  //   18644
  //   3268
  //   3284
  //   4292
  //   4308
  //   5316
  //   5332
  //   11456
  //   11460
  //   11476
  //   2048
  //   2052
  //   2068
  //   6336
  //   7360
  //   22720
  //   23744
  //   8384
  //   9408
  //   10432
  //   1034
  //   1673
  //   6
  //   30
  //   133
  //   149
  //   1030
  //   1669
  //   32792
  //   65560
  //   98328
  //   163864
  //   196632
  //   229400
  //   420
  //   32
  //   36
  //   131096
  //   262148
  //   262172
  //   263176
  //   524932
  //   524948
  //   525960
  //   1048576
  //   24
endmodule
