// Digital circuit ImReg.dig as structural Verilog
module ImReg (
  input  [15:0] inst,
  input  en,
  input  C,
  output [15:0] imm
);

  wire [15:15] register_1_q;

  Register #(.Bits(16)) register_1 (.D(inst), .C(C), .en(en), .Q({register_1_q[15], imm[14:0]}));

  assign imm[15] = inst[8];
endmodule
