// Digital circuit Processor.dig as structural Verilog
module Processor (
  input  Clock
);

  wire alu_1_p6, alu_1_p7, alu_1_p8, branch_1_p5, control_1_p2, control_1_p4, control_1_p5, control_1_p7,
       control_1_p8, control_1_p9, control_1_p10, control_1_p11, control_1_p12, control_1_p13, gpo_1_p5,
       gpo_1_p6, gpo_1_p7, gpo_1_p8, gpo_1_p9, gpo_1_p10, gpo_1_p11, gpo_1_p12, gpo_1_p13, gpo_1_p14,
       gpo_1_p15, gpo_1_p16, gpo_1_p17, gpo_1_p18, gpo_1_p19, gpo_1_p20, register_1_p5, register_1_p6,
       register_1_p7;
  wire [2:0] control_1_p6;
  wire [3:0] rom_1_d, rom_1_d_2;
  wire [6:0] rom_1_d_4;
  wire [8:8] rom_1_d_3;
  wire [15:0] alu_1_p5, driver_1_out, imreg_1_imm, multiplexer_1_out, multiplexer_2_out, pc_1_next, pc_1_pc,
       register_1_p8, register_1_p9, signext_1__5d, signext_1__5s, signext_1__9sd;

  PC pc_1 (.ALU(alu_1_p5), .C(Clock), .abs(control_1_p5), .rel(branch_1_p5), .Next(pc_1_next), .PC(pc_1_pc));
  ROM #(.Bits(16), .Addr_Bits(16)) rom_1 (.A(pc_1_pc), .sel(1'b1), .D({rom_1_d_4, rom_1_d_3[8], rom_1_d_2, rom_1_d}));
  assign driver_1_out = control_1_p2 ? pc_1_next : 16'bz;  // Driver driver_1
  // Register register_1: pin names not known; wires that end beside it: driver_1_out, Clock, rom_1_d, rom_1_d_2, register_1_p5, register_1_p6, register_1_p7, register_1_p8, register_1_p9
  ImReg imreg_1 (.inst({rom_1_d_4, rom_1_d_3[8], rom_1_d_2, rom_1_d}), .en(control_1_p4), .C(Clock), .imm(imreg_1_imm));
  // Control control_1: pin names not known; wires that end beside it: rom_1_d_4, control_1_p2, register_1_p5, control_1_p4, control_1_p5, control_1_p6, control_1_p7, control_1_p8, control_1_p9, control_1_p10, control_1_p11, control_1_p12, control_1_p13
  // Probe R0 on register_1_p6
  SignExt signext_1 (
    .inst({rom_1_d_4, rom_1_d_3[8], rom_1_d_2, rom_1_d}), ._5S(signext_1__5s), ._9SD(signext_1__9sd),
    ._5D(signext_1__5d));
  // Probe R1 on register_1_p7
  Multiplexer #(.Selector_Bits(3), .Bits(16)) multiplexer_1 (
    .sel(control_1_p6), .in_0(register_1_p9), .in_1(imreg_1_imm), .in_2({16{1'b0}}), .in_3(16'hff),
    .in_4(16'hfff), .in_5(signext_1__5s), .in_6(signext_1__9sd), .in_7(signext_1__5d), .out(multiplexer_1_out));
  Multiplexer #(.Bits(16)) multiplexer_2 (
    .sel(control_1_p7), .in_0(register_1_p8), .in_1(register_1_p9), .out(multiplexer_2_out));
  // ALU alu_1: pin names not known; wires that end beside it: multiplexer_2_out, multiplexer_1_out, control_1_p9, Clock, alu_1_p5, alu_1_p6, alu_1_p7, alu_1_p8
  assign driver_1_out = control_1_p8 ? alu_1_p5 : 16'bz;  // Driver driver_2
  // Branch branch_1: pin names not known; wires that end beside it: alu_1_p6, alu_1_p7, alu_1_p8, control_1_p10, branch_1_p5
  RAMDualPort #(.Bits(16), .Addr_Bits(16)) ramdualport_1 (
    .A(alu_1_p5), .Din(register_1_p9), .str(control_1_p11), .C(Clock), .ld(control_1_p12), .D(driver_1_out));
  Terminal terminal_1 (.D(alu_1_p5), .A(register_1_p9), .C(Clock), .W(control_1_p13));
  // GPO gpo_1: pin names not known; wires that end beside it: alu_1_p5, register_1_p9, Clock, control_1_p13, gpo_1_p5, gpo_1_p6, gpo_1_p7, gpo_1_p8, gpo_1_p9, gpo_1_p10, gpo_1_p11, gpo_1_p12, gpo_1_p13, gpo_1_p14, gpo_1_p15, gpo_1_p16, gpo_1_p17, gpo_1_p18, gpo_1_p19, gpo_1_p20
  LED led_1 (.in(gpo_1_p5));
  LED led_2 (.in(gpo_1_p6));
  LED led_3 (.in(gpo_1_p7));
  LED led_4 (.in(gpo_1_p8));
  LED led_5 (.in(gpo_1_p9));
  LED led_6 (.in(gpo_1_p10));
  LED led_7 (.in(gpo_1_p11));
  LED led_8 (.in(gpo_1_p12));
  LED led_9 (.in(gpo_1_p13));
  LED led_10 (.in(gpo_1_p14));
  LED led_11 (.in(gpo_1_p15));
  LED led_12 (.in(gpo_1_p16));
  LED led_13 (.in(gpo_1_p17));
  LED led_14 (.in(gpo_1_p18));
  LED led_15 (.in(gpo_1_p19));
  LED led_16 (.in(gpo_1_p20));

  // Notes on the sheet:
  //   Clock: Hz: 1000
  //   contents of rom_1 (hex, n*v repeats v):
  //   158
  //   5120
  //   21328
  //   21488
  //   5130
  //   21312
  //   21472
  //   32800
  //   4608
  //   21040
  //   21104
  //   21152
  //   21200
  //   21264
  //   21424
  //   32805
  //   4608
  //   21168
  //   21280
  //   21440
  //   32865
  //   4608
  //   21216
  //   32868
  //   4608
  //   21248
  //   32869
  //   4608
  //   21024
  //   21392
  //   32870
  //   4608
  //   21136
  //   32871
  //   4608
  //   21344
  //   32872
  //   4608
  //   21008
  //   32873
  //   4608
  //   21360
  //   32877
  //   4608
  //   21088
  //   32878
  //   4608
  //   21232
  //   32879
  //   4608
  //   21120
  //   32883
  //   4608
  //   21056
  //   21408
  //   32884
  //   4608
  //   20992
  //   32885
  //   4608
  //   21072
  //   32886
  //   4608
  //   21376
  //   32888
  //   4608
  //   21184
  //   21296
  //   21456
  //   5125
  //   8417
  //   19680
  //   5124
  //   8417
  //   19680
  //   5120
  //   8417
  //   19680
  //   8417
  //   32850
  //   4848
  //   19695
  //   28175
  //   6371
  //   5129
  //   8417
  //   19680
  //   5382
  //   8417
  //   19680
  //   8417
  //   32862
  //   4848
  //   19695
  //   28163
  //   6370
  //   31744
  //   28643
  //   8417
  //   19693
  //   734
  //   589
  //   6210
  //   20020
  //   19971
  //   15360
  //   24070
  //   32805
  //   14848
  //   24073
  //   29680
  //   6193
  //   28663
  //   749
  //   20190
  //   6369
  //   20222
  //   6369
  //   27151
  //   6193
  //   19971
  //   32888
  //   14848
  //   25605
  //   6209
  //   19972
  //   32900
  //   26864
  //   28654
  //   32805
  //   4688
  //   29685
  //   28649
  //   18432
  //   18944
  //   32915
  //   26656
  //   18944
  //   32915
  //   26656
  //   18432
  //   18944
  //   32915
  //   26656
  //   18944
  //   32915
  //   26656
  //   27151
  //   528
  //   10271
  //   15386
  //   25091
  //   32816
  //   5648
  //   28162
  //   32823
  //   5648
  //   29681
  //   27138
  //   16
endmodule
