// Digital circuit ProcessorIntr.dig as structural Verilog
// Einfacher Prozessor, der an die MIPS-Architektur 
// angelehnt ist. Es handelt sich um eine Harvard 
// Single-Cycle CPU. Er verfügt über einen Interrupt 
// Controller: Durch eine steigende Flanke am Eingang intr 
// wird ein Interrupt ausgelöst. Dabei wird die feste 
// Adresse 0x1000 angesprungen.
// An dieser Adresse muss sich die ISR befinden.
module ProcessorIntr (
  input  C,
  input  intr,
  output [15:0] D,
  output [15:0] A,
  output ioR,
  output ioW
);

  wire abs, ALU2D, alu_1_p6, alu_1_p7, alu_1_p8, ALUop, br, branch_1_p3, branch_1_p4, branch_1_p5, iEn, imm,
       ld, muxA, pcintr_1_p5, reti, sf, src2D, st, stPC, WE;
  wire [2:0] muxB;
  wire [15:0] imreg_1_p4, multiplexer_1_out, multiplexer_2_out, multiplexer_3_out, next, pcintr_1_p7,
       register_1_p6, register_1_p7, retAddr, rom_1_d, signext_1_p2, signext_1_p3, signext_1_p4;

  Multiplexer #(.Bits(16)) multiplexer_1 (.sel(reti), .in_0(A), .in_1(retAddr), .out(multiplexer_1_out));
  // PCintr pcintr_1: pin names not known; wires that end beside it: multiplexer_1_out, C, abs, iEn, pcintr_1_p5, next, pcintr_1_p7
  ROM #(.AddrBits(16), .isProgramMemory("true"), .Bits(16), .Addr_Bits(16)) rom_1 (
    .A(pcintr_1_p7), .sel(1'b1), .D(rom_1_d));
  assign D = stPC ? next : 16'bz;  // Driver driver_1
  // ControlIntr controlintr_1: pin names not known; wires that end beside it: reti, ioR, ioW, ld, st, br, sf, ALUop, ALU2D, muxA, src2D, muxB, abs, imm, WE, rom_1_d[15:9], stPC
  // Register register_1: pin names not known; wires that end beside it: D, C, rom_1_d[3:0], rom_1_d[7:4], WE, register_1_p6, register_1_p7
  // ImReg imreg_1: pin names not known; wires that end beside it: rom_1_d, imm, C, imreg_1_p4
  // SignExt signext_1: pin names not known; wires that end beside it: rom_1_d, signext_1_p2, signext_1_p3, signext_1_p4
  assign D = src2D ? register_1_p7 : 16'bz;  // Driver driver_2
  Multiplexer #(.Bits(16)) multiplexer_2 (
    .sel(muxA), .in_0(register_1_p6), .in_1(register_1_p7), .out(multiplexer_2_out));
  Multiplexer #(.Selector_Bits(3), .Bits(16)) multiplexer_3 (
    .sel(muxB), .in_0(register_1_p7), .in_1(imreg_1_p4), .in_2({16{1'b0}}), .in_3(16'hff), .in_4(16'hfff),
    .in_5(signext_1_p2), .in_6(signext_1_p3), .in_7(signext_1_p4), .out(multiplexer_3_out));
  // Branch branch_1: pin names not known; wires that end beside it: pcintr_1_p5, br, branch_1_p3, branch_1_p4, branch_1_p5
  // ALU alu_1: pin names not known; wires that end beside it: multiplexer_2_out, multiplexer_3_out, ALUop, branch_1_p3, A, alu_1_p6, alu_1_p7, alu_1_p8
  // Interrupt interrupt_1: pin names not known; wires that end beside it: C, next, pcintr_1_p5, imm, abs, reti, intr, retAddr, iEn
  // FlagsRW flagsrw_1: pin names not known; wires that end beside it: branch_1_p3, branch_1_p4, branch_1_p5, D, ioW, ioR, A, sf, C, alu_1_p8, alu_1_p7, alu_1_p6
  assign D = ALU2D ? A : 16'bz;  // Driver driver_3
  RAMSinglePort #(.AddrBits(16), .Bits(16), .Addr_Bits(16)) ramsingleport_1 (.A(A), .str(st), .C(C), .ld(ld), .D(D));

  // Notes on the sheet:
  //   C: Hz: 500000
  //   D: Datenbus
  //   A: Adressbus
  //   ioR: io Read
  //   ioW: io Write
  //   intr: Interrupt Eingang. Geht diese Leitung auf high wird ein
  //   Interrupt ausgelöst. Die ISR muss sich an Adresse 
  //   0x1000 befinden.
  //   contents of rom_1 (hex, n*v repeats v):
  //   99ab,1200,8015,68f0,8020,1200,73f0,8f8a,1200,8015,68f0,8020,1200,73f0,1831,203,8015,
  //   68f0,140a,73f0,6feb,4800,4a00,8024,6820,4a00,8024,6820,4800,4a00,8024,6820,4a00,8024,
  //   6820,6a0f,210,281f,3c1a,6203,8030,1610,6e02,8037,1610,73f1,6a02,0,0,0,0,0,0,0,0,0,
  //   0,0,0,0,0,0,0,0,0,0,0,0,0,0,0,0,0,0,0,0,0,0,0,0,0,0,0,0,0,0,0,0,0,0,0,0,0,0,0,0,0,
  //   0,0,0,0,0,0,0,0,0,0,0,0,0,0,0,0,0,0,0,0,0,0,0,0,0,0,0,0,0,0,0,0,0,0,0,0,0,0,0,0,0,
  //   0,0,0,0,0,0,0,0,0,0,0,0,0,0,0,0,0,0,0,0,0,0,0,0,0,0,0,0,0,0,0,0,0,0,0,0,0,0,0,0,0,
  //   0,0,0,0,0,0,0,0,0,0,0,0,0,0,0,0,0,0,0,0,0,0,0,0,0,0,0,0,0,0,0,0,0,0,0,0,0,0,0,0,0,
  //   0,0,0,0,0,0,0,0,0,0,0,0,0,0,0,0,0,0,0,0,0,0,0,0,0,0,0,0,0,0,0,0,0,0,0,0,0,0,0,0,0,
  //   0,0,0,0,0,0,0,0,0,0,0,0,0,0,0,0,0,0,0,0,0,0,0,0,0,0,0,0,0,0,0,0,0,0,0,0,0,0,0,0,0,
  //   0,0,0,0,0,0,0,0,0,0,0,0,0,0,0,0,0,0,0,0,0,0,0,0,0,0,0,0,0,0,0,0,0,0,0,0,0,0,0,0,0,
  //   0,0,0,0,0,0,0,0,0,0,0,0,0,0,0,0,0,0,0,0,0,0,0,0,0,0,0,0,0,0,0,0,0,0,0,0,0,0,0,0,0,
  //   0,0,0,0,0,0,0,0,0,0,0,0,0,0,0,0,0,0,0,0,0,0,0,0,0,0,0,0,0,0,0,0,0,0,0,0,0,0,0,0,0,
  //   0,0,0,0,0,0,0,0,0,0,0,0,0,0,0,0,0,0,0,0,0,0,0,0,0,0,0,0,0,0,0,0,0,0,0,0,0,0,0,0,0,
  //   0,0,0,0,0,0,0,0,0,0,0,0,0,0,0,0,0,0,0,0,0,0,0,0,0,0,0,0,0,0,0,0,0,0,0,0,0,0,0,0,0,
  //   0,0,0,0,0,0,0,0,0,0,0,0,0,0,0,0,0,0,0,0,0,0,0,0,0,0,0,0,0,0,0,0,0,0,0,0,0,0,0,0,0,
  //   0,0,0,0,0,0,0,0,0,0,0,0,0,0,0,0,0,0,0,0,0,0,0,0,0,0,0,0,0,0,0,0,0,0,0,0,0,0,0,0,0,
  //   0,0,0,0,0,0,0,0,0,0,0,0,0,0,0,0,0,0,0,0,0,0,0,0,0,0,0,0,0,0,0,0,0,0,0,0,0,0,0,0,0,
  //   0,0,0,0,0,0,0,0,0,0,0,0,0,0,0,0,0,0,0,0,0,0,0,0,0,0,0,0,0,0,0,0,0,0,0,0,0,0,0,0,0,
  //   0,0,0,0,0,0,0,0,0,0,0,0,0,0,0,0,0,0,0,0,0,0,0,0,0,0,0,0,0,0,0,0,0,0,0,0,0,0,0,0,0,
  //   0,0,0,0,0,0,0,0,0,0,0,0,0,0,0,0,0,0,0,0,0,0,0,0,0,0,0,0,0,0,0,0,0,0,0,0,0,0,0,0,0,
  //   0,0,0,0,0,0,0,0,0,0,0,0,0,0,0,0,0,0,0,0,0,0,0,0,0,0,0,0,0,0,0,0,0,0,0,0,0,0,0,0,0,
  //   0,0,0,0,0,0,0,0,0,0,0,0,0,0,0,0,0,0,0,0,0,0,0,0,0,0,0,0,0,0,0,0,0,0,0,0,0,0,0,0,0,
  //   0,0,0,0,0,0,0,0,0,0,0,0,0,0,0,0,0,0,0,0,0,0,0,0,0,0,0,0,0,0,0,0,0,0,0,0,0,0,0,0,0,
  //   0,0,0,0,0,0,0,0,0,0,0,0,0,0,0,0,0,0,0,0,0,0,0,0,0,0,0,0,0,0,0,0,0,0,0,0,0,0,0,0,0,
  //   0,0,0,0,0,0,0,0,0,0,0,0,0,0,0,0,0,0,0,0,0,0,0,0,0,0,0,0,0,0,0,0,0,0,0,0,0,0,0,0,0,
  //   0,0,0,0,0,0,0,0,0,0,0,0,0,0,0,0,0,0,0,0,0,0,0,0,0,0,0,0,0,0,0,0,0,0,0,0,0,0,0,0,0,
  //   0,0,0,0,0,0,0,0,0,0,0,0,0,0,0,0,0,0,0,0,0,0,0,0,0,0,0,0,0,0,0,0,0,0,0,0,0,0,0,0,0,
  //   0,0,0,0,0,0,0,0,0,0,0,0,0,0,0,0,0,0,0,0,0,0,0,0,0,0,0,0,0,0,0,0,0,0,0,0,0,0,0,0,0,
  //   0,0,0,0,0,0,0,0,0,0,0,0,0,0,0,0,0,0,0,0,0,0,0,0,0,0,0,0,0,0,0,0,0,0,0,0,0,0,0,0,0,
  //   0,0,0,0,0,0,0,0,0,0,0,0,0,0,0,0,0,0,0,0,0,0,0,0,0,0,0,0,0,0,0,0,0,0,0,0,0,0,0,0,0,
  //   0,0,0,0,0,0,0,0,0,0,0,0,0,0,0,0,0,0,0,0,0,0,0,0,0,0,0,0,0,0,0,0,0,0,0,0,0,0,0,0,0,
  //   0,0,0,0,0,0,0,0,0,0,0,0,0,0,0,0,0,0,0,0,0,0,0,0,0,0,0,0,0,0,0,0,0,0,0,0,0,0,0,0,0,
  //   0,0,0,0,0,0,0,0,0,0,0,0,0,0,0,0,0,0,0,0,0,0,0,0,0,0,0,0,0,0,0,0,0,0,0,0,0,0,0,0,0,
  //   0,0,0,0,0,0,0,0,0,0,0,0,0,0,0,0,0,0,0,0,0,0,0,0,0,0,0,0,0,0,0,0,0,0,0,0,0,0,0,0,0,
  //   0,0,0,0,0,0,0,0,0,0,0,0,0,0,0,0,0,0,0,0,0,0,0,0,0,0,0,0,0,0,0,0,0,0,0,0,0,0,0,0,0,
  //   0,0,0,0,0,0,0,0,0,0,0,0,0,0,0,0,0,0,0,0,0,0,0,0,0,0,0,0,0,0,0,0,0,0,0,0,0,0,0,0,0,
  //   0,0,0,0,0,0,0,0,0,0,0,0,0,0,0,0,0,0,0,0,0,0,0,0,0,0,0,0,0,0,0,0,0,0,0,0,0,0,0,0,0,
  //   0,0,0,0,0,0,0,0,0,0,0,0,0,0,0,0,0,0,0,0,0,0,0,0,0,0,0,0,0,0,0,0,0,0,0,0,0,0,0,0,0,
  //   0,0,0,0,0,0,0,0,0,0,0,0,0,0,0,0,0,0,0,0,0,0,0,0,0,0,0,0,0,0,0,0,0,0,0,0,0,0,0,0,0,
  //   0,0,0,0,0,0,0,0,0,0,0,0,0,0,0,0,0,0,0,0,0,0,0,0,0,0,0,0,0,0,0,0,0,0,0,0,0,0,0,0,0,
  //   0,0,0,0,0,0,0,0,0,0,0,0,0,0,0,0,0,0,0,0,0,0,0,0,0,0,0,0,0,0,0,0,0,0,0,0,0,0,0,0,0,
  //   0,0,0,0,0,0,0,0,0,0,0,0,0,0,0,0,0,0,0,0,0,0,0,0,0,0,0,0,0,0,0,0,0,0,0,0,0,0,0,0,0,
  //   0,0,0,0,0,0,0,0,0,0,0,0,0,0,0,0,0,0,0,0,0,0,0,0,0,0,0,0,0,0,0,0,0,0,0,0,0,0,0,0,0,
  //   0,0,0,0,0,0,0,0,0,0,0,0,0,0,0,0,0,0,0,0,0,0,0,0,0,0,0,0,0,0,0,0,0,0,0,0,0,0,0,0,0,
  //   0,0,0,0,0,0,0,0,0,0,0,0,0,0,0,0,0,0,0,0,0,0,0,0,0,0,0,0,0,0,0,0,0,0,0,0,0,0,0,0,0,
  //   0,0,0,0,0,0,0,0,0,0,0,0,0,0,0,0,0,0,0,0,0,0,0,0,0,0,0,0,0,0,0,0,0,0,0,0,0,0,0,0,0,
  //   0,0,0,0,0,0,0,0,0,0,0,0,0,0,0,0,0,0,0,0,0,0,0,0,0,0,0,0,0,0,0,0,0,0,0,0,0,0,0,0,0,
  //   0,0,0,0,0,0,0,0,0,0,0,0,0,0,0,0,0,0,0,0,0,0,0,0,0,0,0,0,0,0,0,0,0,0,0,0,0,0,0,0,0,
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endmodule
