// Digital circuit ProcessorTest.dig as structural Verilog
module ProcessorTest (
  input  Clk
);

  Processor processor_1 (.Clock(Clk));

  // Notes on the sheet:
  //   Clk: Hz: 200
endmodule

/* Test case MOV:
# auto generated, do not modify
Clk R1 R2
init R1=3;
init R2=4;
# mov r2,r1
program(0x121)
C X X
0 3 3
# R1=3
# R2=3
*/

/* Test case ADD no carry:
# auto generated, do not modify
Clk Carry R2
init R1=3;
init R2=4;
# add r2,r1
program(0x221)
C X X
0 0 7
# Carry=0
# R2=7
*/

/* Test case ADD carry:
# auto generated, do not modify
Clk Carry R2
init R1=-1;
init R2=-1;
# add r2,r1
program(0x221)
C X X
0 1 65534
# Carry=1
# R2=65534
*/

/* Test case ADC no carry:
# auto generated, do not modify
Clk Carry R2
init R1=3;
init R2=4;
# adc r2,r1
program(0x321)
C X X
0 0 7
# Carry=0
# R2=7
*/

/* Test case ADC carry:
# auto generated, do not modify
Clk Carry R2
init R1=3;
init R2=4;
init Carry=1;
# adc r2,r1
program(0x321)
C X X
0 0 8
# Carry=0
# R2=8
*/

/* Test case ADC carry out:
# auto generated, do not modify
Clk Carry R2
init R1=-1;
init R2=-1;
# adc r2,r1
program(0x321)
C X X
0 1 65534
# Carry=1
# R2=65534
*/

/* Test case ADDI small:
# auto generated, do not modify
Clk R1
init R1=3;
# addi r1,4
program(0xc14)
C X
0 7
# R1=7
*/

/* Test case ADDI large:
# auto generated, do not modify
Clk R1
init R1=3;
# addi r1,20
program(0x8014,0xb10)
repeat (2) C X
0 23
# R1=23
*/

/* Test case ADCI small:
# auto generated, do not modify
Clk R1
init R1=3;
# adci r1,4
program(0xe14)
C X
0 7
# R1=7
*/

/* Test case ADCI large:
# auto generated, do not modify
Clk R1
init R1=3;
# adci r1,20
program(0x8014,0xd10)
repeat (2) C X
0 23
# R1=23
*/

/* Test case ADCI small, carry:
# auto generated, do not modify
Clk R1
init R1=3;
init Carry=1;
# adci r1,4
program(0xe14)
C X
0 8
# R1=8
*/

/* Test case ADCI large, carry:
# auto generated, do not modify
Clk R1
init R1=3;
init Carry=1;
# adci r1,20
program(0x8014,0xd10)
repeat (2) C X
0 24
# R1=24
*/

/* Test case SUB:
# auto generated, do not modify
Clk Carry R2
init R1=3;
init R2=4;
# sub r2,r1
program(0x421)
C X X
0 0 1
# Carry=0
# R2=1
*/

/* Test case SUB carry out:
# auto generated, do not modify
Clk Carry R2
init R1=4;
init R2=3;
# sub r2,r1
program(0x421)
C X X
0 1 65535
# Carry=1
# R2=65535
*/

/* Test case SBC:
# auto generated, do not modify
Clk Carry R2
init R1=3;
init R2=4;
# sbc r2,r1
program(0x521)
C X X
0 0 1
# Carry=0
# R2=1
*/

/* Test case SBC carry in:
# auto generated, do not modify
Clk Carry R2
init R1=3;
init R2=5;
init Carry=1;
# sbc r2,r1
program(0x521)
C X X
0 0 1
# Carry=0
# R2=1
*/

/* Test case SUBI small:
# auto generated, do not modify
Clk R1
init R1=4;
# subi r1,2
program(0x1012)
C X
0 2
# R1=2
*/

/* Test case SUBI large:
# auto generated, do not modify
Clk R1
init R1=30;
# subi r1,20
program(0x8014,0xf10)
repeat (2) C X
0 10
# R1=10
*/

/* Test case SBCI no carry, small:
# auto generated, do not modify
Clk R1
init R1=6;
# sbci r1,4
program(0x1214)
C X
0 2
# R1=2
*/

/* Test case SBCI no carry, large:
# auto generated, do not modify
Clk R1
init R1=30;
# sbci r1,20
program(0x8014,0x1110)
repeat (2) C X
0 10
# R1=10
*/

/* Test case SBCI carry in, small:
# auto generated, do not modify
Clk R1
init R1=6;
init Carry=1;
# sbci r1,4
program(0x1214)
C X
0 1
# R1=1
*/

/* Test case SBCI carry in, large:
# auto generated, do not modify
Clk R1
init R1=30;
init Carry=1;
# sbci r1,20
program(0x8014,0x1110)
repeat (2) C X
0 9
# R1=9
*/

/* Test case NOT:
# auto generated, do not modify
Clk R1
init R1=0;
# not r1
program(0x1a10)
C X
0 65535
# R1=65535
*/

/* Test case NEG:
# auto generated, do not modify
Clk R1
init R1=1;
# neg r1
program(0x1310)
C X
0 65535
# R1=65535
*/

/* Test case SWAP:
# auto generated, do not modify
Clk R1
init R1=4660;
# swap r1
# brk
program(0x2910,0x4400)
repeat (2) C X
0 13330
# R1=13330
*/

/* Test case SWAPN:
# auto generated, do not modify
Clk R1
init R1=4660;
# swapn r1
program(0x2a10)
C X
0 8515
# R1=8515
*/

/* Test case LDI small:
# auto generated, do not modify
Clk R1
# ldi r1,5
program(0xa15)
C X
0 5
# R1=5
*/

/* Test case LDI small:
# auto generated, do not modify
Clk R1
# ldi r1,15
program(0xa1f)
C X
0 15
# R1=15
*/

/* Test case LDI large:
# auto generated, do not modify
Clk R1
# ldi r1,16
program(0x8010,0x910)
repeat (2) C X
0 16
# R1=16
*/

/* Test case LDI large:
# auto generated, do not modify
Clk R1
# ldi r1,0x8000
program(0x8000,0x911)
repeat (2) C X
0 32768
# R1=32768
*/
