// Digital circuit Flags.dig as structural Verilog
// Speichert die Prozessor-Flags. 
// Über den store-Eingang, kann der aktuelle Zustand
// der Flags gespeichert werden. Das Carry-Flag kann 
// dann für arithmetische Funktion genutzt werden,
// alle Flags für eine bedingte Verzweigung.
module Flags (
  input  Zi,
  input  Ni,
  input  Ci,
  input  C,
  input  store,
  output Zo,
  output No,
  output Co
);

  Register Carry (.D(Ci), .C(C), .en(store), .Q(Co));
  Register Zero (.D(Zi), .C(C), .en(store), .Q(Zo));
  Register Neg (.D(Ni), .C(C), .en(store), .Q(No));

  // Notes on the sheet:
  //   Zi: Das Zero-Flag welches gespeichert werden soll.
  //   Zo: Gibt das gespeicherte Zero-Flag aus.
  //   Ni: Das Negative-Flag welches gespeichert werden soll.
  //   No: Gibt das gespeicherte Negative-Flag aus.
  //   Ci: Das Carry-Flag welches gespeichert werden soll.
  //   Co: Gibt das gespeicherte Carry-Flag aus.
  //   C: der Takteingang
  //   store: Der Eingang welcher das Speichern aktiviert. Es wird auf Eins gesetzt, wenn eine arithmetische Operation ausgeführt wird.
endmodule
