// Digital circuit Interrupt.dig as structural Verilog
// Simple interrupt controller.
// If an interrupt is triggered, the controller is disabled: no 
// further interrupts can be triggered. Setting the input reti 
// releases the interrupt controller.
// {{de Einfacher Interrupt-Controller.
// Wird ein Interrupt ausgelöst, wird der Controller
// gesperrt: Es können keine weiteren Interrupts
// ausgelöst werden. Erst der Eingang reti gibt den 
// Interrupt-Controller wieder frei.}}
module Interrupt (
  input  C,
  input  [15:0] intRet,
  input  imm,
  input  reti,
  input  intr,
  output [15:0] retAddr,
  output iEn
);

  wire and_1_out, intLock_nq, rising_1_out;

  Rising rising_1 (.Reset(iEn), .Set(intr), .Out(rising_1_out));
  JK_FF intLock (.J(and_1_out), .C(C), .K(reti), .nQ(intLock_nq));  // open: Q
  and and_1 (and_1_out, intLock_nq, rising_1_out, ~imm);  // And
  Register #(.Bits(16)) u_retAddr (.D(intRet), .C(C), .en(and_1_out), .Q(retAddr));
  D_FF u_iEn (.D(and_1_out), .C(C), .Q(iEn));  // open: nQ

  // Notes on the sheet:
  //   retAddr: Return Address {{de Return Adresse}}
  //   iEn: interrupt trigger used by the PC
  //   {{de Interrupt-Freigabe für PC}}
  //   intRet: The next commands address, that 
  //   is the return address.
  //   {{de Der nächste Befehl, also die 
  //   Rücksprungadresse.}}
  //   imm: immediate register:
  //   If set, an interrupt is blocked.
  //   {{de Immediate Register:
  //   Wenn gesetzt, wird Interrupt verhindert.}}
  //   reti: return from interrupt. This signal is used to 
  //   release the interrupt controller.
  //   {{de return from interrupt. Über dieses Signal werden
  //   die Interrupts wieder freigegeben.}}
  //   intr: interrupt trigger {{de Interrupt Anforderung}}
endmodule
