// Digital circuit SignExt.dig as structural Verilog
// Extracts small constants from the instruction word.
// There can be two 4-bit constants and a sign extended 8-bit 
// constant (the 8 bits of both registers sign extended)
// {{de Extrahiert kleine Konstanten aus dem Befehlswort.
// Es können zwei 4-Bit Konstanten
// und eine vorzeichenerweiterte 8-Bit Konstante (Die 8 Bits beider Register
// mit Vorzeichenerweiterung)}}
module SignExt (
  input  [15:0] inst,
  output [15:0] _4S,
  output [15:0] _8SD,
  output [15:0] _4D
);


  assign _4D = {{12{1'b0}}, inst[7:4]};
  assign _4S = {{12{1'b0}}, inst[3:0]};
  assign _8SD = {{9{inst[7]}}, inst[6:0]};

  // Notes on the sheet:
  //   inst: instruction word
  //   {{de Das Befehlswort}}
  //   _4S: The four bits taken from Rs.
  //   {{de Die vier Bit aus Rs}}
  //   _8SD: The eight bits taken from Rs,Rd with sign extension.
  //   {{de Die acht Bit aus Rs,Rd mit Vorzeichenerweiterung}}
  //   _4D: The four bits taken from Rd.
  //   {{de Die vier Bit aus Rd}}
endmodule
