// Digital circuit RS-MS-Simp.dig as structural Verilog
module RS_MS_Simp (
  input  R,
  input  C,
  input  S,
  output Q,
  output nQ
);

  wire not_1_out, rs_c_1_p4, rs_c_1_p5;

  // RS_C rs_c_1: pin names not known; wires that end beside it: S, C, R, rs_c_1_p4, rs_c_1_p5
  not not_1 (not_1_out, C);
  // RS_C rs_c_2: pin names not known; wires that end beside it: rs_c_1_p4, not_1_out, rs_c_1_p5, Q, nQ
endmodule
