// Digital circuit multip_D_working.dig as structural Verilog
module multip_D_working (
  input  D,
  input  C,
  output Q
);

  wire d_ms_1_q, d_ms_2_q;

  D_MS d_ms_1 (.D(D), .C(C), .Q(d_ms_1_q));  // open: nQ
  D_MS d_ms_2 (.D(d_ms_1_q), .C(C), .Q(d_ms_2_q));  // open: nQ
  D_MS d_ms_3 (.D(d_ms_2_q), .C(C), .Q(Q));  // open: nQ
endmodule
