// Digital circuit ArduinoUnoExample.dig as structural Verilog
module ArduinoUnoExample (
  input  clk,
  output out_1,
  output out_2,
  output out_3,
  output out_4,
  output out_5,
  output out_6,
  output out_7,
  output out_8,
  output out_9,
  output out_10,
  output out_11,
  output out_12,
  output out_13,
  output out_14,
  output out_15,
  output out_16,
  output out_17,
  output out_18,
  output out_19,
  output out_20,
  output [7:0] out_22
);

  wire arduinouno_1_txc, reset_1_out;

  Reset #(.invertOutput("false")) reset_1 (.out(reset_1_out));
  ArduinoUno #(.generic("firmwareFilePath := \"src/test/resources/simavr/test-firmware/firmware.elf\";")) arduinouno_1 (
    .R(reset_1_out), .C(clk), .TxD(out_22), .TxC(arduinouno_1_txc), .D0(out_1), .D1(out_2), .D2(out_3),
    .D3(out_4), .D4(out_5), .D5(out_6), .D6(out_7), .D7(out_8), .D8(out_9), .D9(out_10), .D10(out_11),
    .D11(out_12), .D12(out_13), .D13(out_14), .D14(out_15), .D15(out_16), .D16(out_17), .D17(out_18),
    .D18(out_19), .D19(out_20));
  PullDown pulldown_1 (.out(arduinouno_1_txc));
  Break break_1 (.brk(arduinouno_1_txc));
endmodule
