// Digital circuit cmosSERFFullAdder.dig as structural Verilog
// Static Energy Recovery Full Adder (SERF)
module cmosSERFFullAdder (
  input  A,
  input  B,
  input  C_i,
  output S,
  output C_o
);

  wire pfet_1_d, pfet_2_d, pfet_3_d;

  PFET pfet_1 (.G(A), .S(1'b1), .D(pfet_1_d));
  PFET pfet_2 (.G(B), .S(pfet_1_d), .D(pfet_2_d));
  NFET nfet_1 (.G(B), .D(pfet_2_d), .S(A));
  NFET nfet_2 (.G(A), .D(pfet_2_d), .S(B));
  PFET pfet_3 (.G(C_i), .S(1'b1), .D(pfet_3_d));
  PFET pfet_4 (.G(pfet_2_d), .S(pfet_3_d), .D(S));
  NFET nfet_3 (.G(pfet_2_d), .D(S), .S(C_i));
  NFET nfet_4 (.G(C_i), .D(S), .S(pfet_2_d));
  PFET pfet_5 (.G(pfet_2_d), .S(C_i), .D(C_o));
  NFET nfet_5 (.G(pfet_2_d), .D(C_o), .S(A));
endmodule

/* Test case Failing:
 A   B   C_i  C_o  S
 0   0   0     0   0
 0   0   1     0   1
 0   1   0     0   1
 0   1   1     1   0
 1   0   0     0   1
 1   0   1     1   0
 1   1   0     1   0
 1   1   1     1   1



# transitions
0 0 0 0 0
0 0 1 0 1
0 0 0 0 0
0 1 0 0 1
0 0 0 0 0
0 1 1 1 0
0 0 0 0 0
1 0 0 0 1
0 0 0 0 0
1 0 1 1 0
0 0 0 0 0
1 1 0 1 0
0 0 0 0 0
1 1 1 1 1
0 0 0 0 0
0 0 1 0 1
0 1 0 0 1
0 0 1 0 1
0 1 1 1 0
0 0 1 0 1
1 0 0 0 1
0 0 1 0 1
1 0 1 1 0
0 0 1 0 1
1 1 0 1 0
0 0 1 0 1
1 1 1 1 1
0 0 1 0 1
0 1 0 0 1
0 1 1 1 0
0 1 0 0 1
1 0 0 0 1
0 1 0 0 1
1 0 1 1 0
0 1 0 0 1
1 1 0 1 0
0 1 0 0 1
1 1 1 1 1
0 1 0 0 1
0 1 1 1 0
1 0 0 0 1
0 1 1 1 0
1 0 1 1 0
0 1 1 1 0
1 1 0 1 0
0 1 1 1 0
1 1 1 1 1
0 1 1 1 0
1 0 0 0 1
1 0 1 1 0
1 0 0 0 1
1 1 0 1 0
1 0 0 0 1
1 1 1 1 1
1 0 0 0 1
1 0 1 1 0
1 1 0 1 0
1 0 1 1 0
1 1 1 1 1
1 0 1 1 0
1 1 0 1 0
1 1 1 1 1
1 1 0 1 0
*/
